# Fritzing sketch Magnetic-Stirrer-Fritzing (saved by Fritzing 0.9.3b)
breadboards: 1

parts:
  Power_plug_-_12V = Power plug
  LED1 = LED - 5mm [color="Red (633nm)" package="5 mm [THT]"]
  M1_Fan = DC Motor
  S1_-_Power_Switch = Pushbutton [package=THT]
  R1_-_100_ohm_potmeter = Rotary Potentiometer (Small) [maximum_resistance=100Ω package=THT]
  R1 = Resistor [tolerance=±5% resistance=68 package=THT]
  S1 = Pushbutton [package=THT]
  R2 = Resistor [tolerance=±5% resistance=68 package=THT]
  S2 = Pushbutton [package=THT]
  R3 = Resistor [tolerance=±5% resistance=0 package=THT]
  R4 = Resistor [tolerance=±5% resistance=470 package=THT]
  S3 = Pushbutton [package=THT]
  R5 = Resistor [tolerance=±5% resistance=68 package=THT]

nets:
  N1: Power_plug_-_12V.GND, LED1.cathode, M1_Fan.pin_2, R1_-_100_ohm_potmeter.leg1, R3.Pin_0
  N2: Power_plug_-_12V.VCC, S1_-_Power_Switch.leg0, S1.leg0, S2.leg0, S3.leg0
  N3: LED1.anode, R4.Pin_1
  N4: M1_Fan.pin_1, R1_-_100_ohm_potmeter.wiper, R4.Pin_0
  N5: S1_-_Power_Switch.leg1, R1_-_100_ohm_potmeter.leg2
  N6: R1.Pin_0, R2.Pin_0, R3.Pin_1, R5.Pin_0
  N7: R1.Pin_1, S1.leg1
  N8: R2.Pin_1, S2.leg1
  N9: S3.leg1, R5.Pin_1

notes:
  12V power supply
  Fan
  Fan Switch
  Potmeter
  Indicator LED
  Heating Pad Switches & Resistors
  Heating Pad
